# Fritzing sketch ionic-ardubot (saved by Fritzing 0.9.2b)
breadboards: 1

parts:
  Componente1 = Arduino Pro Mini v13
  IC1 = L293D [package=THT]  # not connected

nets:
  N1: Componente1.DTR, Componente1.D0/TX
